# Fritzing sketch GM5516_Sketch (saved by Fritzing 0.9.4)
breadboards: 1

parts:
  U1 = NodeMCU V1.0
  R1 = Resistor [tolerance=±5% resistance=220 package=THT]
  LDR = Photocell (LDR) [package=THT]

nets:
  N1: U1.GND, R1.Pin_0
  N2: U1.3V3, LDR.pin_0
  N3: U1.A0, R1.Pin_1, LDR.pin_1

custom parts:
  NodeMCU V1.0: ESP8266 based NodeMCU

// code stored in the sketch: Untitled.ino
void setup()
{
  Serial.begin(9600);
}
void loop()
{
  int sensorValue = analogRead(A0);
  float voltage = sensorValue;
  Serial.print("voltage = ");
  Serial.println(voltage);
  delay(500);
}
